# Fritzing sketch esquema (saved by Fritzing 0.9.3b)
breadboards: 1

parts:
  Componente1 = Arduino Uno (Rev3) - ICSP
  U1 = ESP8266 WiFi Module [part_number=ESP8266]
  part = DHT11 Humitidy and Temperature Sensor
  part_2 = DHT11 Humitidy and Temperature Sensor
  L298N1 = L298N DC motor driver
  BAT1 = 12 battery [package=battery]
  M1 = RioRand LM2596
  R1 = Resistor [tolerance=±5% resistance=220 package="1206 [SMD]"]

nets:
  N1: Componente1.D4, L298N1.IN2
  N2: Componente1.D5_PWM, L298N1.IN1
  N3: Componente1.D6_PWM, U1.GPIO_2, part_2.DATA
  N4: Componente1.D7, U1.GPIO_0, part.DATA
  3V3: Componente1.3V3, U1.VCC
  VDD: Componente1.5V, part.VDD, part_2.VDD
  GND: Componente1.GND, U1.GND, part.GND, part_2.GND
  N5: L298N1.OUT1, M1.Pin_2
  N6: L298N1.12V, BAT1.+
  N7: L298N1.GND, BAT1.-
  N8: M1.Pin_3, R1.Pin_1
  N9: M1.Pin_4, R1.Pin_0

custom parts:
  ESP8266 WiFi Module: Generic WiFi Module based on the ESP8266 with onboard PCB antenna and UART communications
  DHT11 Humitidy and Temperature Sensor: DHT11 Humidity and Temperature Sensor
  L298N DC motor driver: 2x DC motor driver with 78M05 positive voltage regulator (7..35 V) L298N: max 46 V, 2 A Set 5 V Enable jumper to enable 5 V regultor (needed for the L298N) and +5 V output at screw terminal or supply external +5 V at screw terminal Set ENA and/or ENB to +5 V to enable motor permanently or supply ENA and/or ENB with PWM signal IN1 and IN2 set rotation directory for motor A (OUT1/OUT2) IN2 and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
  12 battery: 12V lead acid type battery, like the Husqvarna YTH2448 12V 35AH battery. This is the mini version 1/4 the size of the actual battery to be closer to typical breadboard parts (around 2in wide rathher than 7in). The pads in pcb are sized to accomidate up to 14ga wire (as these batterys will deliver high currents.)
